# Fritzing sketch fritzing schéma (saved by Fritzing 0.9.2b)
breadboards: 1

parts:
  Composant1 = Arduino Uno (Rev3)
  U3 = POT [package=pot_mammoth]
  S1 = Momentary Switch [package=ksa_sealed_tac_switch]
  LED1 = LEDs [package=led10mm]
  U7 = PIC-ICSP [package=molex-1x6_lock]  # not connected
  R1 = Resistor [tolerance=±5% resistance=1k package=THT]
  U8 = LM386 [package=dip08]
  R2 = Resistor [tolerance=±5% resistance=1k package=THT]
  R1_2 = Resistor [tolerance=±5% resistance=1k package=THT]
  C4 = Electrolytic Capacitor [capacitance=100µF package="300 mil [THT, electrolytic]"]  # not connected

nets (from the breadboard view):
  N1: Composant1.A5/SCL, U3.A
  N2: Composant1.D2, S1.2
  N3: Composant1.D3_PWM, R1.Pin_0
  N4: Composant1.D4, LED1.A
  N5: Composant1.5V, U3.E, S1.4, LED1.C, U8.V+
  N6: Composant1.GND, U3.S
  N7: U8.GAIN, U8.+IN, R1_2.Pin_0
  N8: U8.-IN, R2.Pin_1, R1_2.Pin_1
  N9: U8.OUT, R2.Pin_0

notes:
  pédale
  commande manuelle
